// Logisim project Buffered_Output.circ as structural Verilog: 1 circuit, main circuit main
module main (
  input  [9:0] PACKET_IN,
  input  READ_MODE,
  input  WRITE_EN,
  input  READ_EN,
  input  RESET,
  input  CLK,
  output [9:0] PACKET_OUT,
  output FULL,
  output [3:0] COUNT,
  output EMPTY
);

  FIFO_main main_1 (
    .DATA_IN(PACKET_IN), .READ_MODE(READ_MODE), .WRITE_EN(WRITE_EN), .READ_EN(READ_EN), .RESET(RESET),
    .CLK(CLK), .DATA_OUT(PACKET_OUT), .FULL(FULL), .COUNT(COUNT), .EMPTY(EMPTY));
endmodule
