// Logisim project Complete_Buffered_Packet_Router.circ as structural Verilog: 1 circuit, main circuit main
module main (
  input  [9:0] PACKET_IN,
  input  VALID_IN,
  input  [3:0] READY_OUT,
  input  RESET,
  input  CLK,
  output [9:0] PACKET_OUT_0,
  output [9:0] PACKET_OUT_1,
  output [9:0] PACKET_OUT_2,
  output [9:0] PACKET_OUT_3,
  output READY_IN,
  output [3:0] VALID_OUT
);

  wire Destination_Decoder_out0, Destination_Decoder_out1, Destination_Decoder_out2,
       Destination_Decoder_out3, or_1_out;
  wire [1:0] Packet_Input_destination;
  wire [3:0] Flow_Control_read_en, Flow_Control_write_en, main_1_empty_0, main_1_full_0;

  Packet_Input Packet_Input (.Packet(PACKET_IN), .Destination(Packet_Input_destination));  // open: Data
  Destination_Decoder Destination_Decoder (
    .in_1(Packet_Input_destination), .OUT0(Destination_Decoder_out0), .OUT1(Destination_Decoder_out1),
    .OUT2(Destination_Decoder_out2), .OUT3(Destination_Decoder_out3));
  Flow_Control_main Flow_Control (
    .VALID_IN(VALID_IN), .FULL(main_1_full_0), .DESTINATION(Packet_Input_destination),
    .EMPTY(main_1_empty_0), .READY_OUT(READY_OUT), .WRITE_EN(Flow_Control_write_en), .READY_IN(READY_IN),
    .VALID_OUT(VALID_OUT), .READ_EN(Flow_Control_read_en));
  or or_1 (or_1_out, Flow_Control_write_en[0], Flow_Control_write_en[1], Flow_Control_write_en[2], Flow_Control_write_en[3]);
  Four_Output_FIFOs_main main_1 (
    .PACKET_IN(PACKET_IN), .WRITE_EN(or_1_out), .READ_MODE_0(1'b1), .READ_EN_0(Flow_Control_read_en[0]),
    .READ_MODE_1(1'b1), .READ_EN_1(Flow_Control_read_en[1]), .READ_MODE_2(1'b1),
    .READ_EN_2(Flow_Control_read_en[2]), .READ_MODE_3(1'b1), .READ_EN_3(Flow_Control_read_en[3]),
    .RESET(RESET), .CLK(CLK), .PACKET_OUT_0(PACKET_OUT_0), .FULL_0(main_1_full_0[0]),
    .EMPTY_0(main_1_empty_0[0]), .PACKET_OUT_1(PACKET_OUT_1), .FULL_1(main_1_full_0[1]),
    .EMPTY_1(main_1_empty_0[1]), .PACKET_OUT_2(PACKET_OUT_2), .FULL_2(main_1_full_0[2]),
    .EMPTY_2(main_1_empty_0[2]), .PACKET_OUT_3(PACKET_OUT_3), .FULL_3(main_1_full_0[3]),
    .EMPTY_3(main_1_empty_0[3]));
endmodule
