// Logisim project Data_Router.circ as structural Verilog: 2 circuits, main circuit Data_Channel
module Data_Channel (
  input  [7:0] Data,
  input  Enable,
  output [7:0] DATA_OUT
);

  and and_1 (DATA_OUT[0], Data[0], Enable);
  and and_2 (DATA_OUT[1], Data[1], Enable);
  and and_3 (DATA_OUT[2], Data[2], Enable);
  and and_4 (DATA_OUT[3], Data[3], Enable);
  and and_5 (DATA_OUT[4], Data[4], Enable);
  and and_6 (DATA_OUT[5], Data[5], Enable);
  and and_7 (DATA_OUT[6], Data[6], Enable);
  and and_8 (DATA_OUT[7], Data[7], Enable);
endmodule

module Data_Router (
  input  [7:0] Data,
  input  E0,
  input  E1,
  input  E2,
  input  E3,
  output [7:0] DATA_OUT0,
  output [7:0] DATA_OUT1,
  output [7:0] DATA_OUT2,
  output [7:0] DATA_OUT3
);

  Data_Channel data_channel_1 (.Data(Data), .Enable(E0), .DATA_OUT(DATA_OUT0));
  Data_Channel data_channel_2 (.Data(Data), .Enable(E1), .DATA_OUT(DATA_OUT1));
  Data_Channel data_channel_3 (.Data(Data), .Enable(E2), .DATA_OUT(DATA_OUT2));
  Data_Channel data_channel_4 (.Data(Data), .Enable(E3), .DATA_OUT(DATA_OUT3));
endmodule
