// Logisim project Destination_Decoder.circ as structural Verilog: 1 circuit, main circuit Destination_Decoder
module Destination_Decoder (
  input  [1:0] in_1,
  output OUT0,
  output OUT1,
  output OUT2,
  output OUT3
);

  wire not_1_out, not_2_out;

  not not_1 (not_1_out, in_1[1]);
  not not_2 (not_2_out, in_1[0]);
  and and_1 (OUT0, not_1_out, not_2_out);
  and and_2 (OUT1, not_1_out, in_1[0]);
  and and_3 (OUT2, in_1[1], not_2_out);
  and and_4 (OUT3, in_1[1], in_1[0]);
endmodule
