// Logisim project Flow_Control.circ as structural Verilog: 3 circuits, main circuit main
module main (
  input  VALID_IN,
  input  [3:0] FULL,
  input  [1:0] DESTINATION,
  input  [3:0] EMPTY,
  input  [3:0] READY_OUT,
  output [3:0] WRITE_EN,
  output READY_IN,
  output [3:0] VALID_OUT,
  output [3:0] READ_EN
);

  Write_Side Write_Side (
    .VALID_IN(VALID_IN), .FULL(FULL), .DESTINATION(DESTINATION), .WRITE_EN(WRITE_EN), .READY_IN(READY_IN));
  Read_Side Read_Side (.EMPTY(EMPTY), .READY_OUT(READY_OUT), .VALID_OUT(VALID_OUT), .READ_EN(READ_EN));
endmodule

module Write_Side (
  input  VALID_IN,
  input  [3:0] FULL,
  input  [1:0] DESTINATION,
  output [3:0] WRITE_EN,
  output READY_IN
);

  wire and_5_out, and_6_out, and_7_out, and_8_out, destination_decoder_1_out0, destination_decoder_1_out1,
       destination_decoder_1_out2, destination_decoder_1_out3, not_1_out, not_2_out, not_3_out, not_4_out;

  Destination_Decoder destination_decoder_1 (
    .in_1(DESTINATION), .OUT0(destination_decoder_1_out0), .OUT1(destination_decoder_1_out1),
    .OUT2(destination_decoder_1_out2), .OUT3(destination_decoder_1_out3));
  not not_1 (not_1_out, FULL[0]);
  not not_2 (not_2_out, FULL[1]);
  not not_3 (not_3_out, FULL[2]);
  not not_4 (not_4_out, FULL[3]);
  and and_1 (WRITE_EN[0], VALID_IN, not_1_out, destination_decoder_1_out0);
  and and_2 (WRITE_EN[1], VALID_IN, not_2_out, destination_decoder_1_out1);
  and and_3 (WRITE_EN[2], VALID_IN, not_3_out, destination_decoder_1_out2);
  and and_4 (WRITE_EN[3], VALID_IN, not_4_out, destination_decoder_1_out3);
  and and_5 (and_5_out, not_1_out, destination_decoder_1_out0);
  and and_6 (and_6_out, not_2_out, destination_decoder_1_out1);
  and and_7 (and_7_out, not_3_out, destination_decoder_1_out2);
  and and_8 (and_8_out, not_4_out, destination_decoder_1_out3);
  or or_1 (READY_IN, and_5_out, and_6_out, and_7_out, and_8_out);
endmodule

module Read_Side (
  input  [3:0] EMPTY,
  input  [3:0] READY_OUT,
  output [3:0] VALID_OUT,
  output [3:0] READ_EN
);

  not not_1 (VALID_OUT[0], EMPTY[0]);
  not not_2 (VALID_OUT[1], EMPTY[1]);
  not not_3 (VALID_OUT[2], EMPTY[2]);
  not not_4 (VALID_OUT[3], EMPTY[3]);
  and and_1 (READ_EN[0], VALID_OUT[0], READY_OUT[0]);
  and and_2 (READ_EN[1], VALID_OUT[1], READY_OUT[1]);
  and and_3 (READ_EN[2], VALID_OUT[2], READY_OUT[2]);
  and and_4 (READ_EN[3], VALID_OUT[3], READY_OUT[3]);
endmodule
