// Logisim project Four_Output_FIFOs.circ as structural Verilog: 1 circuit, main circuit main
module main (
  input  [9:0] PACKET_IN,
  input  WRITE_EN,
  input  READ_MODE_0,
  input  READ_EN_0,
  input  READ_MODE_1,
  input  READ_EN_1,
  input  READ_MODE_2,
  input  READ_EN_2,
  input  READ_MODE_3,
  input  READ_EN_3,
  input  RESET,
  input  CLK,
  output [9:0] PACKET_OUT_0,
  output FULL_0,
  output EMPTY_0,
  output [9:0] PACKET_OUT_1,
  output FULL_1,
  output EMPTY_1,
  output [9:0] PACKET_OUT_2,
  output FULL_2,
  output EMPTY_2,
  output [9:0] PACKET_OUT_3,
  output FULL_3,
  output EMPTY_3
);

  wire and_1_out, and_2_out, and_3_out, and_4_out, destination_decoder_1_out0, destination_decoder_1_out1,
       destination_decoder_1_out2, destination_decoder_1_out3;
  wire [1:0] packet_input_1_destination;
  wire [3:0] Buffered_OUT_0_count, Buffered_OUT_1_count, Buffered_OUT_2_count, Buffered_OUT_3_count;

  Packet_Input packet_input_1 (.Packet(PACKET_IN), .Destination(packet_input_1_destination));  // open: Data
  Destination_Decoder destination_decoder_1 (
    .in_1(packet_input_1_destination), .OUT0(destination_decoder_1_out0), .OUT1(destination_decoder_1_out1),
    .OUT2(destination_decoder_1_out2), .OUT3(destination_decoder_1_out3));
  and and_1 (and_1_out, WRITE_EN, destination_decoder_1_out0);
  and and_2 (and_2_out, WRITE_EN, destination_decoder_1_out1);
  and and_3 (and_3_out, WRITE_EN, destination_decoder_1_out2);
  and and_4 (and_4_out, WRITE_EN, destination_decoder_1_out3);
  Buffered_Output_main Buffered_OUT_0 (
    .PACKET_IN(PACKET_IN), .READ_MODE(READ_MODE_0), .WRITE_EN(and_1_out), .READ_EN(READ_EN_0), .RESET(RESET),
    .CLK(CLK), .PACKET_OUT(PACKET_OUT_0), .FULL(FULL_0), .COUNT(Buffered_OUT_0_count), .EMPTY(EMPTY_0));
  Buffered_Output_main Buffered_OUT_1 (
    .PACKET_IN(PACKET_IN), .READ_MODE(READ_MODE_1), .WRITE_EN(and_2_out), .READ_EN(READ_EN_1), .RESET(RESET),
    .CLK(CLK), .PACKET_OUT(PACKET_OUT_1), .FULL(FULL_1), .COUNT(Buffered_OUT_1_count), .EMPTY(EMPTY_1));
  Buffered_Output_main Buffered_OUT_2 (
    .PACKET_IN(PACKET_IN), .READ_MODE(READ_MODE_2), .WRITE_EN(and_3_out), .READ_EN(READ_EN_2), .RESET(RESET),
    .CLK(CLK), .PACKET_OUT(PACKET_OUT_2), .FULL(FULL_2), .COUNT(Buffered_OUT_2_count), .EMPTY(EMPTY_2));
  Buffered_Output_main Buffered_OUT_3 (
    .PACKET_IN(PACKET_IN), .READ_MODE(READ_MODE_3), .WRITE_EN(and_4_out), .READ_EN(READ_EN_3), .RESET(RESET),
    .CLK(CLK), .PACKET_OUT(PACKET_OUT_3), .FULL(FULL_3), .COUNT(Buffered_OUT_3_count), .EMPTY(EMPTY_3));
endmodule
