// Logisim project Packet_Input.circ as structural Verilog: 1 circuit, main circuit Packet_Input
module Packet_Input (
  input  [9:0] Packet,
  output [1:0] Destination,
  output [7:0] Data
);


  assign Data = Packet[7:0];
  assign Destination = Packet[9:8];
endmodule
