// Logisim project Packet_Router.circ as structural Verilog: 1 circuit, main circuit main
module main (
  input  [9:0] Data,
  output [7:0] ROUTER_OUT0,
  output [7:0] ROUTER_OUT1,
  output [7:0] ROUTER_OUT2,
  output [7:0] ROUTER_OUT3
);

  wire Destination_Decoder_out0, Destination_Decoder_out1, Destination_Decoder_out2, Destination_Decoder_out3;
  wire [1:0] packet_input_1_destination;
  wire [7:0] packet_input_1_data;

  Packet_Input packet_input_1 (.Packet(Data), .Destination(packet_input_1_destination), .Data(packet_input_1_data));
  Destination_Decoder Destination_Decoder (
    .in_1(packet_input_1_destination), .OUT0(Destination_Decoder_out0), .OUT1(Destination_Decoder_out1),
    .OUT2(Destination_Decoder_out2), .OUT3(Destination_Decoder_out3));
  Data_Router Data_Router (
    .Data(packet_input_1_data), .E0(Destination_Decoder_out0), .E1(Destination_Decoder_out1),
    .E2(Destination_Decoder_out2), .E3(Destination_Decoder_out3), .DATA_OUT0(ROUTER_OUT0),
    .DATA_OUT1(ROUTER_OUT1), .DATA_OUT2(ROUTER_OUT2), .DATA_OUT3(ROUTER_OUT3));
endmodule
